# Fritzing sketch 362project (saved by Fritzing 0.9.1b)
breadboards: 1

parts:
  Part1 = Arduino Uno (Rev3)
  LED1 = RGB LED - (4 legs) [package="5 mm [THT]"]
  R1 = Resistor [tolerance=±5% resistance=330 package=THT]
  R2 = Resistor [tolerance=±5% resistance=330 package=THT]
  R3 = Resistor [tolerance=±5% resistance=330 package=THT]
  R5 = Resistor [tolerance=±5% resistance=10k package="1206 [SMD]"]

nets:
  N1: Part1.D2, R5.Pin_0
  N2: Part1.D3_PWM, R2.Pin_0
  N3: Part1.D4, R1.Pin_0
  N4: Part1.D5_PWM, R3.Pin_0
  N5: Part1.5V, LED1.common_anode
  N6: LED1.red_cathode, R2.Pin_1
  N7: LED1.green_cathode, R1.Pin_1
  N8: LED1.blue_cathode, R3.Pin_1

notes:
  1x4 Keypad Membrane
  [G][1][2][3][4]
  Magnet Switch

// code stored in the sketch: 362project.ino
/*

1x4 Keypad from Adafruit.com (Unofficial Source) 
Original Source: Button
Referenced Tutorial on Arduino.com: http://arduino.cc/en/Tutorial/InputPullupSerial
Referenced: http://arduino.cc/en/Reference/pinMode

Turns on and off specified Pin or Prints to Serial Monitor when keys are press 
on a 1x4 keypad from Adafruit.com

*/

// constants won't change. They're used here to
// set pin numbers:
const int buttonPin[] = {9,10,11,12};     // the number of the pushbutton pins
const int ledPin =  13;      // the number of the LED pin

// variables will change:
int buttonState = 0;         // variable for reading the pushbutton status

void setup() {
  // initialize the LED pin as an output:
  pinMode(ledPin, OUTPUT);  
  // initialize the Serial Monitor @ 9600
  Serial.begin(9600);  
  // initialize the keypad pin(s) as an input:
  for(int x=0; x<4; x++)
  {
    pinMode(buttonPin[x], INPUT_PULLUP); 
  }
}

void loop(){
  // read the state of the keypad value:
  for(int x=0; x<4; x++)
  {
    //signifying the state of which the button is in by reading the appropriate pin #
    buttonState = digitalRead(buttonPin[x]);
    
    // check if the pushbutton on the keypad is pressed.
    // if it is, the buttonState is LOW:
  

	//button 1
    if (buttonState == LOW && buttonPin[x] == 10) {
      // turn LED on:
      Serial.print("BTN 1 ON *");
      digitalWrite(ledPin, HIGH);
    }

  	//button 2
    if (buttonState == LOW && buttonPin[x] == 9) {    
      // turn LED off:   
      Serial.print("BTN 2 OFF * ");
      digitalWrite(ledPin, LOW); 
    }

	//button 3
    if (buttonState == LOW && buttonPin[x] == 12) {    
      // turn LED off:   
      Serial.print("BTN 3 ON * ");
      digitalWrite(ledPin, HIGH); 
    }
	
	//button 4
    if (buttonState == LOW && buttonPin[x] == 11) {    
      // turn LED off:   
      Serial.print("BTN 4 OFF * ");
      digitalWrite(ledPin, LOW); 
    }

  }
  delay(100);
}
